# Fritzing sketch DirectionalPadAndLED (saved by Fritzing 0.7.11b)
breadboards: 1

parts:
  LED1 = LED - 5mm [color="Red (633nm)" package="5 mm [THT]"]
  S1 = Pushbutton [package="[THT]"]
  S2 = Pushbutton [package="[THT]"]
  S3 = Pushbutton [package="[THT]"]
  S4 = Pushbutton [package="[THT]"]
  Arduino2 = Arduino
  R5 = Resistor [tolerance=±5% resistance=10k package=THT]
  R6 = Resistor [tolerance=±5% resistance=10k package=THT]
  R7 = Resistor [tolerance=±5% resistance=10k package=THT]
  R8 = Resistor [tolerance=±5% resistance=10k package=THT]

nets:
  N1: LED1.cathode, Arduino2.GND, R6.Pin_0, R7.Pin_0, R8.Pin_0
  N2: LED1.anode, Arduino2.D13
  N3: S1.Pin_1, S1.Pin_2, Arduino2.D5, R8.Pin_1
  N4: S1.Pin_3, S1.Pin_4, S2.Pin_3, S2.Pin_4, S3.Pin_3, S3.Pin_4, S4.Pin_3, S4.Pin_4, Arduino2.+5V, R5.Pin_0
  N5: S2.Pin_1, S2.Pin_2, Arduino2.D7, R7.Pin_1
  N6: S3.Pin_1, S3.Pin_2, Arduino2.D4, R5.Pin_1
  N7: S4.Pin_1, S4.Pin_2, Arduino2.D6, R6.Pin_1

notes:
  A little crazy! Requires an intermediate jumper to get enough room for the resistor.
