# Fritzing sketch ServoMotor (saved by Fritzing 0.7.11b)
breadboards: 1

parts:
  Arduino1 = Arduino
  J1 = Basic Servo

nets:
  N1: Arduino1.D13, J1.pulse
  +5V: Arduino1.+5V, J1.vcc
  GND: Arduino1.GND, J1.gnd
