# Fritzing sketch BasicSpeakerCircuit (saved by Fritzing 0.7.11b)

parts:
  Arduino1 = Arduino
  R2 = Rotary Potentiometer (Small) [maximum_resistance=100kΩ]
  SPKR1 = Loudspeaker
  Arduino2 = Arduino
  R3 = Rotary Potentiometer (Small) [maximum_resistance=100kΩ]
  SPKR2 = Loudspeaker
  C1 = Ceramic Capacitor [capacitance=0.1µF package="100 mil [THT, multilayer]"]

nets:
  N1: Arduino1.GND, SPKR1.pin1
  N2: Arduino1.D13, R2.leg2
  N3: R2.wiper, SPKR1.pin2
  N4: Arduino2.GND, R3.wiper, SPKR2.pin1
  N5: Arduino2.D13, SPKR2.pin2, C1.0
  N6: R3.leg1, C1.1

notes:
  Potentiometer for volume control - try switching the digital pin to the left pin on the potentiometer and see what happens!
  Tone control! The square waves from your Arduino can be harsh (lots of extra harmonics) - a tone knob sends some of those frequencies to ground, making a mellower tone.
  A 0.022uF capacitor will give a standard electric-guitar tone range, but try up to a 0.1uF for much more high-frequency cutoff.
